// Logisim project practica2y3.circ as structural Verilog: 7 circuits, main circuit main
module main (
);

  wire and_1_out_3, and_2_out_3, not_1_out_2, not_2_out_2, not_3_out_2, or_1_out_3, or_2_out_3;

  Not not_1 (.in_1(1'b1), .out_2(not_1_out_2));
  Not not_2 (.in_1(1'b1), .out_2(not_2_out_2));
  Not not_3 (.in_1(1'b1), .out_2(not_3_out_2));
  Or or_1 (.in_1(not_1_out_2), .in_2(1'b1), .out_3(or_1_out_3));
  And and_1 (.in_1(1'b1), .in_2(not_2_out_2), .out_3(and_1_out_3));
  And and_2 (.in_1(not_3_out_2), .in_2(1'b1), .out_3(and_2_out_3));
  Or or_2 (.in_1(and_1_out_3), .in_2(and_2_out_3), .out_3(or_2_out_3));
  LED led_1 (.in(or_1_out_3));
  LED led_2 (.in(or_2_out_3));

  // Notes on the sheet:
  //   1
  //   2
  //   A
  //   B
endmodule

module And (
  input  in_1,
  input  in_2,
  output out_3
);

  wire transistor_1_out;

  Transistor #(.\type ("n")) transistor_1 (.in(1'b1), .out(transistor_1_out), .gate(in_2));
  Transistor transistor_2 (.in(1'b0), .out(out_3), .gate(in_2));
  Transistor transistor_3 (.in(1'b0), .out(out_3), .gate(in_1));
  Transistor #(.\type ("n")) transistor_4 (.in(transistor_1_out), .out(out_3), .gate(in_1));
endmodule

module Or (
  input  in_1,
  input  in_2,
  output out_3
);

  Transistor #(.\type ("n")) transistor_1 (.in(1'b1), .out(out_3), .gate(in_1));
  Transistor transistor_2 (.in(in_2), .out(out_3), .gate(in_1));
endmodule

module Not (
  input  in_1,
  output out_2
);

  Transistor transistor_1 (.in(1'b1), .out(out_2), .gate(in_1));
  Transistor #(.\type ("n")) transistor_2 (.in(1'b0), .out(out_2), .gate(in_1));
endmodule

module primos (
  input  N3,
  input  N2,
  input  N1,
  input  N0,
  output Es_primo
);

  wire and_1_out_3, and_2_out_3, and_3_out_3, and_4_out_3, and_5_out_3, and_6_out_3, and_7_out_3,
       not_1_out_2, not_2_out_2, not_3_out_2, not_4_out_2, not_5_out_2, or_1_out_3, or_2_out_3;

  Not not_1 (.in_1(N3), .out_2(not_1_out_2));
  Not not_2 (.in_1(N3), .out_2(not_2_out_2));
  Not not_3 (.in_1(N2), .out_2(not_3_out_2));
  Not not_4 (.in_1(N2), .out_2(not_4_out_2));
  And and_1 (.in_1(N1), .in_2(not_4_out_2), .out_3(and_1_out_3));
  Not not_5 (.in_1(N1), .out_2(not_5_out_2));
  And and_2 (.in_1(N0), .in_2(and_1_out_3), .out_3(and_2_out_3));
  And and_3 (.in_1(not_5_out_2), .in_2(N2), .out_3(and_3_out_3));
  And and_4 (.in_1(N1), .in_2(and_5_out_3), .out_3(and_4_out_3));
  And and_5 (.in_1(not_1_out_2), .in_2(not_3_out_2), .out_3(and_5_out_3));
  And and_6 (.in_1(N0), .in_2(not_2_out_2), .out_3(and_6_out_3));
  And and_7 (.in_1(N0), .in_2(and_3_out_3), .out_3(and_7_out_3));
  Or or_1 (.in_1(and_4_out_3), .in_2(and_6_out_3), .out_3(or_1_out_3));
  Or or_2 (.in_1(and_2_out_3), .in_2(and_7_out_3), .out_3(or_2_out_3));
  Or or_3 (.in_1(or_1_out_3), .in_2(or_2_out_3), .out_3(Es_primo));
endmodule

module complemento (
  input  N2,
  input  N1,
  input  N0,
  output N2_2,
  output N1_2,
  output N0_2
);

  wire and_1_out_3, and_2_out_3, and_3_out_3, and_4_out_3, and_5_out_3, and_6_out_3, and_7_out_3,
       not_1_out_2, not_2_out_2, not_3_out_2, or_1_out_3;

  Not not_1 (.in_1(N2), .out_2(not_1_out_2));
  And and_1 (.in_1(N1), .in_2(not_1_out_2), .out_3(and_1_out_3));
  And and_2 (.in_1(not_2_out_2), .in_2(not_1_out_2), .out_3(and_2_out_3));
  Or or_1 (.in_1(and_4_out_3), .in_2(and_1_out_3), .out_3(or_1_out_3));
  Or or_2 (.in_1(and_5_out_3), .in_2(or_1_out_3), .out_3(N2_2));
  And and_3 (.in_1(not_2_out_2), .in_2(N2), .out_3(and_3_out_3));
  And and_4 (.in_1(N0), .in_2(and_2_out_3), .out_3(and_4_out_3));
  And and_5 (.in_1(not_3_out_2), .in_2(and_3_out_3), .out_3(and_5_out_3));
  And and_6 (.in_1(not_3_out_2), .in_2(N1), .out_3(and_6_out_3));
  Or or_3 (.in_1(and_7_out_3), .in_2(and_6_out_3), .out_3(N1_2));
  Not not_2 (.in_1(N1), .out_2(not_2_out_2));
  And and_7 (.in_1(N0), .in_2(not_2_out_2), .out_3(and_7_out_3));
  Not not_3 (.in_1(N0), .out_2(not_3_out_2));

  assign N0_2 = N0;
endmodule

module Planta (
  input  in_1,
  input  in_2,
  input  in_3
);

  wire and_1_out_3, and_2_out_3, and_3_out_3, and_4_out_3, and_5_out_3, and_6_out_3, and_7_out_3,
       and_8_out_3, and_9_out_3, not_1_out_2, not_2_out_2, not_3_out_2, not_4_out_2, not_5_out_2,
       not_6_out_2, not_7_out_2, not_8_out_2, not_9_out_2, or_1_out_3, or_2_out_3, or_3_out_3, or_4_out_3;

  Or or_1 (.in_1(in_3), .in_2(in_2), .out_3(or_1_out_3));
  Not not_1 (.in_1(in_1), .out_2(not_1_out_2));
  Not not_2 (.in_1(in_1), .out_2(not_2_out_2));
  Or or_2 (.in_1(or_1_out_3), .in_2(in_1), .out_3(or_2_out_3));
  Not not_3 (.in_1(in_3), .out_2(not_3_out_2));
  Not not_4 (.in_1(in_2), .out_2(not_4_out_2));
  Not not_5 (.in_1(in_3), .out_2(not_5_out_2));
  Not not_6 (.in_1(in_2), .out_2(not_6_out_2));
  Not not_7 (.in_1(or_4_out_3), .out_2(not_7_out_2));
  Or or_3 (.in_1(not_3_out_2), .in_2(not_4_out_2), .out_3(or_3_out_3));
  And and_1 (.in_1(not_5_out_2), .in_2(not_6_out_2), .out_3(and_1_out_3));
  And and_2 (.in_1(or_2_out_3), .in_2(not_7_out_2), .out_3(and_2_out_3));
  And and_3 (.in_1(not_4_out_2), .in_2(not_3_out_2), .out_3(and_3_out_3));
  And and_4 (.in_1(or_3_out_3), .in_2(not_1_out_2), .out_3(and_4_out_3));
  And and_5 (.in_1(and_1_out_3), .in_2(not_2_out_2), .out_3(and_5_out_3));
  Not not_8 (.in_1(and_8_out_3), .out_2(not_8_out_2));
  Or or_4 (.in_1(and_3_out_3), .in_2(and_4_out_3), .out_3(or_4_out_3));
  And and_6 (.in_1(and_2_out_3), .in_2(not_8_out_2), .out_3(and_6_out_3));
  And and_7 (.in_1(in_3), .in_2(in_2), .out_3(and_7_out_3));
  And and_8 (.in_1(and_7_out_3), .in_2(in_1), .out_3(and_8_out_3));
  Not not_9 (.in_1(and_5_out_3), .out_2(not_9_out_2));
  And and_9 (.in_1(or_4_out_3), .in_2(not_9_out_2), .out_3(and_9_out_3));
  LED led_1 (.in(and_8_out_3));
  LED led_2 (.in(and_6_out_3));
  LED led_3 (.in(and_9_out_3));
  LED led_4 (.in(and_5_out_3));

  // Notes on the sheet:
  //   Todo Bien
  //   Servicio Tecnico necesita revisar
  //   Hoy hay que salir mas temprano
  //   Panico. Nada funciona
endmodule
