// Logisim project practica4.circ as structural Verilog
module bit_equal (
  input  in_1,
  input  in_2,
  output out_3
);

  xnor xnor_1 (out_3, in_1, in_2);
endmodule

module _3bit_equal (
  input  in_1,
  input  in_2,
  input  in_3,
  input  in_4,
  input  in_5,
  input  in_6,
  output out_7
);

  wire bit_equal_1_out_3, bit_equal_2_out_3, bit_equal_3_out_3;

  bit_equal bit_equal_1 (.in_1(in_1), .in_2(in_2), .out_3(bit_equal_1_out_3));
  bit_equal bit_equal_2 (.in_1(in_3), .in_2(in_4), .out_3(bit_equal_2_out_3));
  bit_equal bit_equal_3 (.in_1(in_5), .in_2(in_6), .out_3(bit_equal_3_out_3));
  and and_1 (out_7, bit_equal_1_out_3, bit_equal_2_out_3, bit_equal_3_out_3);
endmodule

module bit_add (
  input  in_1,
  input  in_2,
  input  in_3,
  output out_4,
  output out_5
);

  wire and_1_out, and_2_out, xor_1_out;

  and and_1 (and_1_out, in_3, in_2);
  xor xor_1 (xor_1_out, in_2, in_3);
  and and_2 (and_2_out, xor_1_out, in_1);
  xor xor_2 (out_4, in_1, xor_1_out);
  or or_1 (out_5, and_2_out, and_1_out);
endmodule

module ALU (
  input  A,
  input  B,
  input  C_i,
  input  Op,
  input  in_5,
  input  in_6,
  output S,
  output C_i_1
);

  wire and_1_out, and_2_out, and_3_out, and_4_out, and_5_out, bit_add_1_out_4, bit_add_1_out_5,
       n3bit_equal_1_out_7, n3bit_equal_2_out_7, n3bit_equal_3_out_7, n3bit_equal_4_out_7, nor_1_out,
       or_1_out, or_3_out, or_4_out;

  _3bit_equal u_3bit_equal_1 (
    .in_2(Op), .in_4(in_5), .in_6(in_6), .out_7(n3bit_equal_1_out_7), .in_1(1'b0), .in_3(1'b0), .in_5(1'b0));
  _3bit_equal u_3bit_equal_2 (
    .in_2(Op), .in_4(in_5), .in_6(in_6), .out_7(n3bit_equal_2_out_7), .in_1(1'b0), .in_3(1'b0), .in_5(1'b1));
  _3bit_equal u_3bit_equal_3 (
    .in_2(Op), .in_4(in_5), .in_6(in_6), .out_7(n3bit_equal_3_out_7), .in_1(1'b0), .in_3(1'b1), .in_5(1'b0));
  _3bit_equal u_3bit_equal_4 (
    .in_2(Op), .in_4(in_5), .in_6(in_6), .out_7(n3bit_equal_4_out_7), .in_1(1'b1), .in_3(1'b1), .in_5(1'b0));
  bit_add bit_add_1 (.in_2(A), .in_3(B), .out_4(bit_add_1_out_4), .out_5(bit_add_1_out_5), .in_1(C_i));
  and and_1 (and_1_out, B, A);
  or or_1 (or_1_out, B, A);
  nor nor_1 (nor_1_out, B, A);
  or or_2 (S, and_2_out, or_3_out);
  and and_2 (and_2_out, n3bit_equal_1_out_7, and_1_out);
  or or_3 (or_3_out, and_3_out, or_4_out);
  and and_3 (and_3_out, n3bit_equal_2_out_7, or_1_out);
  or or_4 (or_4_out, and_4_out, and_5_out);
  and and_4 (and_4_out, n3bit_equal_3_out_7, nor_1_out);
  and and_5 (and_5_out, n3bit_equal_4_out_7, bit_add_1_out_4);
  and and_6 (C_i_1, n3bit_equal_4_out_7, bit_add_1_out_5);
endmodule

module _8_bit_ALU (
  input  in_1,
  input  in_2,
  input  in_3,
  input  in_4,
  input  in_5,
  input  in_6,
  input  in_7,
  input  in_8,
  input  in_9,
  input  in_10,
  input  in_11,
  input  in_12,
  input  in_13,
  input  in_14,
  input  in_15,
  input  in_16,
  input  in_17,
  input  in_18,
  input  in_19,
  output out_20,
  output out_21,
  output out_22,
  output out_23,
  output out_24,
  output out_25,
  output out_26,
  output out_27,
  output out_28
);

  wire alu_1_c_i_1, alu_2_c_i_1, alu_3_c_i_1, alu_4_c_i_1, alu_5_c_i_1, alu_6_c_i_1, alu_7_c_i_1;

  ALU alu_1 (.A(in_4), .B(in_5), .C_i(1'b0), .Op(in_1), .in_5(in_2), .in_6(in_3), .S(out_20), .C_i_1(alu_1_c_i_1));
  ALU alu_2 (
    .A(in_6), .B(in_7), .C_i(alu_1_c_i_1), .Op(in_1), .in_5(in_2), .in_6(in_3), .S(out_21),
    .C_i_1(alu_2_c_i_1));
  ALU alu_3 (
    .A(in_8), .B(in_9), .C_i(alu_2_c_i_1), .Op(in_1), .in_5(in_2), .in_6(in_3), .S(out_22),
    .C_i_1(alu_3_c_i_1));
  ALU alu_4 (
    .A(in_10), .B(in_11), .C_i(alu_3_c_i_1), .Op(in_1), .in_5(in_2), .in_6(in_3), .S(out_23),
    .C_i_1(alu_4_c_i_1));
  ALU alu_5 (
    .A(in_12), .B(in_13), .C_i(alu_4_c_i_1), .Op(in_1), .in_5(in_2), .in_6(in_3), .S(out_24),
    .C_i_1(alu_5_c_i_1));
  ALU alu_6 (
    .A(in_14), .B(in_15), .C_i(alu_5_c_i_1), .Op(in_1), .in_5(in_2), .in_6(in_3), .S(out_25),
    .C_i_1(alu_6_c_i_1));
  ALU alu_7 (
    .A(in_16), .B(in_17), .C_i(alu_6_c_i_1), .Op(in_1), .in_5(in_2), .in_6(in_3), .S(out_26),
    .C_i_1(alu_7_c_i_1));
  ALU alu_8 (.A(in_18), .B(in_19), .C_i(alu_7_c_i_1), .Op(in_1), .in_5(in_2), .in_6(in_3), .S(out_27), .C_i_1(out_28));
endmodule

module ALU_2 (
  input  in_1,
  input  in_2,
  input  in_3,
  input  B,
  input  in_5,
  input  in_6,
  input  in_7,
  input  in_8,
  input  in_9,
  input  in_10,
  input  in_11,
  input  in_12,
  input  in_13,
  input  in_14,
  input  in_15,
  input  in_16,
  input  in_17,
  input  in_18,
  input  in_19,
  output out_20,
  output out_21,
  output out_22,
  output out_23,
  output out_24,
  output out_25,
  output out_26,
  output out_27,
  output out_28
);

  wire n3bit_equal_1_out_7, n8_bit_alu_1_out_20, n8_bit_alu_1_out_21, n8_bit_alu_1_out_22,
       n8_bit_alu_1_out_23, n8_bit_alu_1_out_24, n8_bit_alu_1_out_25, n8_bit_alu_1_out_26,
       n8_bit_alu_1_out_27, xor_1_out, xor_2_out, xor_3_out, xor_4_out, xor_5_out, xor_6_out, xor_7_out,
       xor_8_out, xor_9_out;

  _3bit_equal u_3bit_equal_1 (
    .in_2(in_3), .in_4(in_2), .in_6(in_1), .out_7(n3bit_equal_1_out_7), .in_1(1'b1), .in_3(1'b1), .in_5(1'b1));
  xor xor_1 (xor_1_out, n3bit_equal_1_out_7, B);
  xor xor_2 (xor_2_out, n3bit_equal_1_out_7, in_5);
  xor xor_3 (xor_3_out, n3bit_equal_1_out_7, in_6);
  xor xor_4 (xor_4_out, n3bit_equal_1_out_7, in_8);
  xor xor_5 (xor_5_out, n3bit_equal_1_out_7, in_11);
  xor xor_6 (xor_6_out, n3bit_equal_1_out_7, in_14);
  xor xor_7 (xor_7_out, n3bit_equal_1_out_7, in_17);
  xor xor_8 (xor_8_out, n3bit_equal_1_out_7, in_19);
  _8_bit_ALU u_8_bit_alu_1 (
    .in_4(n3bit_equal_1_out_7), .in_5(xor_1_out), .in_6(1'b0), .in_7(xor_2_out), .in_10(1'b0),
    .in_11(xor_4_out), .in_12(1'b0), .in_13(xor_5_out), .in_14(1'b0), .in_15(xor_6_out), .in_16(1'b0),
    .in_17(xor_7_out), .out_20(n8_bit_alu_1_out_20), .out_21(n8_bit_alu_1_out_21),
    .out_23(n8_bit_alu_1_out_23), .out_24(n8_bit_alu_1_out_24), .out_25(n8_bit_alu_1_out_25),
    .out_26(n8_bit_alu_1_out_26), .in_1(1'b1), .in_2(1'b1), .in_3(1'b0), .in_8(1'b0),
    .out_22(n8_bit_alu_1_out_22), .in_9(xor_3_out), .in_18(1'b0), .out_27(n8_bit_alu_1_out_27),
    .in_19(xor_8_out));  // open: out_28
  xor xor_9 (xor_9_out, n3bit_equal_1_out_7, in_3);
  _8_bit_ALU u_8_bit_alu_2 (
    .in_4(n8_bit_alu_1_out_20), .in_5(in_7), .in_6(n8_bit_alu_1_out_21), .in_7(in_9),
    .in_10(n8_bit_alu_1_out_23), .in_11(in_12), .in_12(n8_bit_alu_1_out_24), .in_13(in_13),
    .in_14(n8_bit_alu_1_out_25), .in_15(in_15), .in_16(n8_bit_alu_1_out_26), .in_17(in_16), .out_20(out_20),
    .out_21(out_21), .out_23(out_23), .out_24(out_24), .out_25(out_25), .out_26(out_26), .in_1(in_1),
    .in_2(in_2), .in_3(xor_9_out), .out_28(out_28), .in_8(n8_bit_alu_1_out_22), .out_22(out_22),
    .in_9(in_10), .in_18(n8_bit_alu_1_out_27), .out_27(out_27), .in_19(in_18));
endmodule

module ALU_2_2 (
  input  in_1,
  input  in_2,
  input  in_3,
  input  in_4,
  input  in_5,
  input  in_6,
  input  A,
  input  in_8,
  input  in_9,
  input  in_10,
  input  in_11,
  input  in_12,
  input  in_13,
  input  in_14,
  input  in_15,
  input  in_16,
  input  in_17,
  input  in_18,
  input  in_19,
  output out_20,
  output out_21,
  output out_22,
  output out_23,
  output out_24,
  output out_25,
  output out_26,
  output out_27,
  output out_28
);

  wire alu_1_out_20, alu_1_out_21, alu_1_out_22, alu_1_out_23, alu_1_out_24, alu_1_out_25, alu_1_out_26,
       alu_1_out_27, alu_2_out_20, alu_2_out_21, alu_2_out_22, alu_2_out_23, alu_2_out_24, alu_2_out_25,
       alu_2_out_26, alu_2_out_27, alu_3_out_20, alu_3_out_21, alu_3_out_22, alu_3_out_23, alu_3_out_24,
       alu_3_out_25, alu_3_out_26, alu_3_out_27, and_1_out, bit_equal_1_out_3, bit_equal_2_out_3,
       bit_equal_3_out_3, bit_equal_4_out_3, bit_equal_5_out_3, bit_equal_6_out_3, bit_equal_7_out_3,
       bit_equal_8_out_3, n3bit_equal_1_out_7, n3bit_equal_2_out_7, n3bit_equal_3_out_7, nor_1_out;

  _3bit_equal u_3bit_equal_1 (
    .in_2(in_1), .in_4(in_2), .in_6(in_3), .out_7(n3bit_equal_1_out_7), .in_1(1'b0), .in_3(1'b1), .in_5(1'b1));
  _3bit_equal u_3bit_equal_2 (
    .in_2(in_1), .in_4(in_2), .in_6(in_3), .out_7(n3bit_equal_2_out_7), .in_1(1'b1), .in_3(1'b0), .in_5(1'b0));
  _3bit_equal u_3bit_equal_3 (
    .in_2(in_1), .in_4(in_2), .in_6(in_3), .out_7(n3bit_equal_3_out_7), .in_1(1'b1), .in_3(1'b0), .in_5(1'b1));
  nor nor_1 (nor_1_out, n3bit_equal_3_out_7, n3bit_equal_2_out_7, n3bit_equal_1_out_7);
  bit_equal bit_equal_1 (.in_1(in_19), .in_2(in_11), .out_3(bit_equal_1_out_3));
  bit_equal bit_equal_2 (.in_1(in_18), .in_2(in_10), .out_3(bit_equal_2_out_3));
  bit_equal bit_equal_3 (.in_1(in_17), .in_2(in_9), .out_3(bit_equal_3_out_3));
  bit_equal bit_equal_4 (.in_1(in_16), .in_2(in_8), .out_3(bit_equal_4_out_3));
  bit_equal bit_equal_5 (.in_1(in_15), .in_2(A), .out_3(bit_equal_5_out_3));
  bit_equal bit_equal_6 (.in_1(in_14), .in_2(in_6), .out_3(bit_equal_6_out_3));
  bit_equal bit_equal_7 (.in_1(in_13), .in_2(in_5), .out_3(bit_equal_7_out_3));
  bit_equal bit_equal_8 (.in_1(in_12), .in_2(in_4), .out_3(bit_equal_8_out_3));
  and and_1 (and_1_out, bit_equal_1_out_3, bit_equal_2_out_3, bit_equal_3_out_3, bit_equal_4_out_3, bit_equal_5_out_3, bit_equal_6_out_3, bit_equal_7_out_3, bit_equal_8_out_3);
  _8_bit_transistor u_8_bit_transistor_1 (
    .in_2(alu_1_out_20), .in_3(alu_1_out_21), .in_4(alu_1_out_22), .in_5(alu_1_out_23), .in_6(alu_1_out_24),
    .in_7(alu_1_out_25), .in_8(alu_1_out_26), .in_9(alu_1_out_27), .out_10(out_27), .out_12(out_25),
    .out_13(out_24), .out_14(out_23), .out_15(out_22), .out_16(out_21), .out_17(out_20),
    .in_1(n3bit_equal_1_out_7), .out_11(out_26));  // open: out_18
  ALU_2 alu_1 (
    .B(in_11), .in_5(in_10), .in_6(in_9), .in_7(in_19), .in_8(in_8), .in_9(in_18), .in_10(in_17), .in_11(A),
    .in_12(in_16), .in_13(in_15), .in_14(in_6), .in_15(in_14), .in_16(in_13), .in_17(in_5), .in_18(in_12),
    .in_19(in_4), .out_20(alu_1_out_20), .out_21(alu_1_out_21), .out_22(alu_1_out_22), .out_23(alu_1_out_23),
    .out_24(alu_1_out_24), .out_25(alu_1_out_25), .out_26(alu_1_out_26), .out_27(alu_1_out_27), .in_1(1'b1),
    .in_2(1'b1), .in_3(1'b1));  // open: out_28
  _8_bit_transistor u_8_bit_transistor_2 (
    .in_2(alu_2_out_20), .in_3(alu_2_out_21), .in_4(alu_2_out_22), .in_5(alu_2_out_23), .in_6(alu_2_out_24),
    .in_7(alu_2_out_25), .in_8(alu_2_out_26), .in_9(alu_2_out_27), .out_10(out_27), .out_12(out_25),
    .out_13(out_24), .out_14(out_23), .out_15(out_22), .out_16(out_21), .out_17(out_20),
    .in_1(n3bit_equal_2_out_7), .out_11(out_26));  // open: out_18
  ALU_2 alu_2 (
    .B(in_19), .in_5(in_18), .in_6(in_17), .in_7(in_11), .in_8(in_16), .in_9(in_10), .in_10(in_9),
    .in_11(in_15), .in_12(in_8), .in_13(A), .in_14(in_14), .in_15(in_6), .in_16(in_5), .in_17(in_13),
    .in_18(in_4), .in_19(in_12), .out_20(alu_2_out_20), .out_21(alu_2_out_21), .out_22(alu_2_out_22),
    .out_23(alu_2_out_23), .out_24(alu_2_out_24), .out_25(alu_2_out_25), .out_26(alu_2_out_26),
    .out_27(alu_2_out_27), .in_1(1'b1), .in_2(1'b1), .in_3(1'b1));  // open: out_28
  _8_bit_transistor u_8_bit_transistor_3 (
    .in_2(and_1_out), .in_3(1'b0), .in_4(1'b0), .in_5(1'b0), .in_6(1'b0), .in_7(1'b0), .in_8(1'b0),
    .in_9(1'b0), .out_10(out_27), .out_12(out_25), .out_13(out_24), .out_14(out_23), .out_15(out_22),
    .out_16(out_21), .out_17(out_20), .in_1(n3bit_equal_3_out_7), .out_11(out_26));  // open: out_18
  ALU_2 alu_3 (
    .B(in_19), .in_5(in_18), .in_6(in_17), .in_7(in_11), .in_8(in_16), .in_9(in_10), .in_10(in_9),
    .in_11(in_15), .in_12(in_8), .in_13(A), .in_14(in_14), .in_15(in_6), .in_16(in_5), .in_17(in_13),
    .in_18(in_4), .in_19(in_12), .out_20(alu_3_out_20), .out_21(alu_3_out_21), .out_22(alu_3_out_22),
    .out_23(alu_3_out_23), .out_24(alu_3_out_24), .out_25(alu_3_out_25), .out_26(alu_3_out_26),
    .out_27(alu_3_out_27), .out_28(out_28), .in_1(in_1), .in_2(in_2), .in_3(in_3));
  _8_bit_transistor u_8_bit_transistor_4 (
    .in_2(alu_3_out_20), .in_3(alu_3_out_21), .in_4(alu_3_out_22), .in_5(alu_3_out_23), .in_6(alu_3_out_24),
    .in_7(alu_3_out_25), .in_8(alu_3_out_26), .in_9(alu_3_out_27), .out_10(out_27), .out_12(out_25),
    .out_13(out_24), .out_14(out_23), .out_15(out_22), .out_16(out_21), .out_17(out_20), .in_1(nor_1_out),
    .out_11(out_26));  // open: out_18

  // Notes on the sheet:
  //   B
endmodule

module _8_bit_transistor (
  input  in_1,
  input  in_2,
  input  in_3,
  input  in_4,
  input  in_5,
  input  in_6,
  input  in_7,
  input  in_8,
  input  in_9,
  output out_10,
  output out_11,
  output out_12,
  output out_13,
  output out_14,
  output out_15,
  output out_16,
  output out_17,
  output out_18
);

  Transistor #(.\type ("n")) transistor_1 (.in(in_2), .out(out_10), .gate(in_1));
  Transistor #(.\type ("n")) transistor_2 (.in(in_3), .out(out_11), .gate(in_1));
  Transistor #(.\type ("n")) transistor_3 (.in(in_4), .out(out_12), .gate(in_1));
  Transistor #(.\type ("n")) transistor_4 (.in(in_5), .out(out_13), .gate(in_1));
  Transistor #(.\type ("n")) transistor_5 (.in(in_6), .out(out_14), .gate(in_1));
  Transistor #(.\type ("n")) transistor_6 (.in(in_7), .out(out_15), .gate(in_1));
  Transistor #(.\type ("n")) transistor_7 (.in(in_8), .out(out_16), .gate(in_1));
  Transistor #(.\type ("n")) transistor_8 (.in(in_9), .out(out_17), .gate(in_1));

  assign out_18 = in_1;
endmodule

module _8_bit_memory (
  input  Clk,
  input  [7:0] Register,
  output [7:0] out_3
);

  wire not_1_out, not_2_out, not_3_out, not_4_out, not_5_out, not_6_out, not_7_out, not_8_out;

  J_K_Flip_Flop j_k_ff_1 (.J(Register[0]), .clk(Clk), .K(not_1_out), .Q(out_3[0]));  // open: Qn, preset, en, reset
  not not_1 (not_1_out, Register[0]);
  J_K_Flip_Flop j_k_ff_2 (.J(Register[1]), .clk(Clk), .K(not_2_out), .Q(out_3[1]));  // open: Qn, preset, en, reset
  not not_2 (not_2_out, Register[1]);
  J_K_Flip_Flop j_k_ff_3 (.J(Register[2]), .clk(Clk), .K(not_3_out), .Q(out_3[2]));  // open: Qn, preset, en, reset
  not not_3 (not_3_out, Register[2]);
  J_K_Flip_Flop j_k_ff_4 (.J(Register[3]), .clk(Clk), .K(not_4_out), .Q(out_3[3]));  // open: Qn, preset, en, reset
  not not_4 (not_4_out, Register[3]);
  J_K_Flip_Flop j_k_ff_5 (.J(Register[4]), .clk(Clk), .K(not_5_out), .Q(out_3[4]));  // open: Qn, preset, en, reset
  not not_5 (not_5_out, Register[4]);
  J_K_Flip_Flop j_k_ff_6 (.J(Register[5]), .clk(Clk), .K(not_6_out), .Q(out_3[5]));  // open: Qn, preset, en, reset
  not not_6 (not_6_out, Register[5]);
  J_K_Flip_Flop j_k_ff_7 (.J(Register[6]), .clk(Clk), .K(not_7_out), .Q(out_3[6]));  // open: Qn, preset, en, reset
  not not_7 (not_7_out, Register[6]);
  J_K_Flip_Flop j_k_ff_8 (.J(Register[7]), .clk(Clk), .K(not_8_out), .Q(out_3[7]));  // open: Qn, preset, en, reset
  not not_8 (not_8_out, Register[7]);
endmodule

module ALU_Spliter (
  input  [2:0] in_1,
  input  [7:0] A,
  input  [7:0] B,
  output [7:0] out_4,
  output Desborde
);

  ALU_2_2 alu_1 (
    .in_1(in_1[2]), .in_2(in_1[1]), .in_3(in_1[0]), .in_4(A[7]), .in_5(A[6]), .in_6(A[5]), .A(A[4]),
    .in_8(A[3]), .in_9(A[2]), .in_10(A[1]), .in_11(A[0]), .in_12(B[7]), .in_13(B[6]), .in_14(B[5]),
    .in_15(B[4]), .in_16(B[3]), .in_17(B[2]), .in_18(B[1]), .in_19(B[0]), .out_20(out_4[7]),
    .out_21(out_4[6]), .out_22(out_4[5]), .out_23(out_4[4]), .out_24(out_4[3]), .out_25(out_4[2]),
    .out_26(out_4[1]), .out_27(out_4[0]), .out_28(Desborde));
endmodule

module automata (
  input  ln,
  input  in_2,
  input  in_3
);

  wire and_1_out, and_2_out, clock_1_out, not_1_out, or_1_out, S1_q, S1_qn, S2_q, S2_qn;

  not not_1 (not_1_out, ln);
  and and_1 (and_1_out, S1_qn, ln);
  Clock clock_1 (.out(clock_1_out));
  and and_2 (and_2_out, S1_q, not_1_out);
  or or_1 (or_1_out, and_1_out, and_2_out);
  D_Flip_Flop S1 (.clk(clock_1_out), .D(or_1_out), .Q(S1_q), .Qn(S1_qn), .en(in_2));  // open: preset, reset
  D_Flip_Flop S2 (.clk(clock_1_out), .D(S2_qn), .Q(S2_q), .Qn(S2_qn), .en(in_3));  // open: preset, reset

  // Notes on the sheet:
  //   E1
  //   E2
  //   Estados
  //   PP=00
  //   IP=01
  //   II=10
  //   PI=11
endmodule

module registro (
  input  in_1,
  input  enable,
  output out_3,
  output out_4
);

  wire clock_1_out, not_1_out, s_r_ff_1_q, s_r_ff_1_qn, s_r_ff_2_q, s_r_ff_2_qn, s_r_ff_3_q, s_r_ff_3_qn,
       s_r_ff_4_q, s_r_ff_4_qn, s_r_ff_5_q, s_r_ff_5_qn, s_r_ff_6_q, s_r_ff_6_qn, s_r_ff_7_q, s_r_ff_7_qn;

  Clock clock_1 (.out(clock_1_out));
  not not_1 (not_1_out, in_1);
  S_R_Flip_Flop s_r_ff_1 (
    .S(s_r_ff_2_q), .clk(clock_1_out), .R(s_r_ff_2_qn), .Q(s_r_ff_1_q), .Qn(s_r_ff_1_qn), .en(enable));  // open: preset, reset
  S_R_Flip_Flop s_r_ff_2 (
    .S(in_1), .clk(clock_1_out), .R(not_1_out), .Q(s_r_ff_2_q), .Qn(s_r_ff_2_qn), .reset(enable), .en(enable));  // open: preset
  S_R_Flip_Flop s_r_ff_3 (
    .S(s_r_ff_1_q), .clk(clock_1_out), .R(s_r_ff_1_qn), .Q(s_r_ff_3_q), .Qn(s_r_ff_3_qn), .en(enable));  // open: preset, reset
  S_R_Flip_Flop s_r_ff_4 (
    .S(s_r_ff_3_q), .clk(clock_1_out), .R(s_r_ff_3_qn), .Q(s_r_ff_4_q), .Qn(s_r_ff_4_qn), .en(enable));  // open: preset, reset
  S_R_Flip_Flop s_r_ff_5 (
    .S(s_r_ff_6_q), .clk(clock_1_out), .R(s_r_ff_6_qn), .Q(s_r_ff_5_q), .Qn(s_r_ff_5_qn), .en(enable));  // open: preset, reset
  S_R_Flip_Flop s_r_ff_6 (
    .S(s_r_ff_4_q), .clk(clock_1_out), .R(s_r_ff_4_qn), .Q(s_r_ff_6_q), .Qn(s_r_ff_6_qn), .en(enable));  // open: preset, reset
  S_R_Flip_Flop s_r_ff_7 (
    .S(s_r_ff_5_q), .clk(clock_1_out), .R(s_r_ff_5_qn), .Q(s_r_ff_7_q), .Qn(s_r_ff_7_qn), .en(enable));  // open: preset, reset
  S_R_Flip_Flop s_r_ff_8 (
    .S(s_r_ff_7_q), .clk(clock_1_out), .R(s_r_ff_7_qn), .Q(out_3), .Qn(out_4), .en(enable));  // open: preset, reset
endmodule

module registro_paralelo (
  input  in_1,
  input  in_2,
  input  [7:0] in_3,
  output [7:0] out_4
);

  wire not_1_out, not_2_out, not_3_out, not_4_out, not_5_out, not_6_out, not_7_out, not_8_out;

  S_R_Flip_Flop s_r_ff_1 (.S(in_3[0]), .clk(in_1), .R(not_1_out), .Q(out_4[0]), .en(in_2));  // open: Qn, preset, reset
  not not_1 (not_1_out, in_3[0]);
  S_R_Flip_Flop s_r_ff_2 (.S(in_3[1]), .clk(in_1), .R(not_2_out), .Q(out_4[1]), .en(in_2));  // open: Qn, preset, reset
  not not_2 (not_2_out, in_3[1]);
  S_R_Flip_Flop s_r_ff_3 (.S(in_3[2]), .clk(in_1), .R(not_3_out), .Q(out_4[2]), .en(in_2));  // open: Qn, preset, reset
  not not_3 (not_3_out, in_3[2]);
  S_R_Flip_Flop s_r_ff_4 (.S(in_3[3]), .clk(in_1), .R(not_4_out), .Q(out_4[3]), .en(in_2));  // open: Qn, preset, reset
  not not_4 (not_4_out, in_3[3]);
  S_R_Flip_Flop s_r_ff_5 (.S(in_3[4]), .clk(in_1), .R(not_5_out), .Q(out_4[4]), .en(in_2));  // open: Qn, preset, reset
  not not_5 (not_5_out, in_3[4]);
  S_R_Flip_Flop s_r_ff_6 (.S(in_3[5]), .clk(in_1), .R(not_6_out), .Q(out_4[5]), .en(in_2));  // open: Qn, preset, reset
  not not_6 (not_6_out, in_3[5]);
  S_R_Flip_Flop s_r_ff_7 (.S(in_3[6]), .clk(in_1), .R(not_7_out), .Q(out_4[6]), .en(in_2));  // open: Qn, preset, reset
  not not_7 (not_7_out, in_3[6]);
  S_R_Flip_Flop s_r_ff_8 (.S(in_3[7]), .clk(in_1), .R(not_8_out), .Q(out_4[7]), .en(in_2));  // open: Qn, preset, reset
  not not_8 (not_8_out, in_3[7]);
endmodule

module banco_registros (
  input  [1:0] L1,
  input  [7:0] Registro,
  input  [1:0] E1,
  input  E,
  input  [1:0] L2,
  output [7:0] out_6,
  output [7:0] out_7
);

  wire n2bit_equal_1_out_3, n2bit_equal_2_out_3, n2bit_equal_3_out_3, n2bit_equal_4_out_3,
       n2bit_equal_5_out_3, n2bit_equal_6_out_3, n2bit_equal_7_out_3, n2bit_equal_8_out_3,
       n2bit_equal_9_out_3, n2bit_equal_10_out_3, n2bit_equal_11_out_3, n2bit_equal_12_out_3;
  wire [7:0] registro_paralelo_1_out_4, registro_paralelo_2_out_4, registro_paralelo_3_out_4,
       registro_paralelo_4_out_4, transistor_1_out, transistor_2_out, transistor_3_out, transistor_4_out;

  _2bit_equal u_2bit_equal_1 (.out_3(n2bit_equal_1_out_3), .in_1(E1), .in_2(2'b00));
  Transistor #(.\type ("n"), .width(8)) transistor_1 (
    .in(Registro), .out(transistor_1_out), .gate(n2bit_equal_1_out_3));
  registro_paralelo registro_paralelo_1 (
    .in_3(transistor_1_out), .out_4(registro_paralelo_1_out_4), .in_1(E));  // open: in_2
  _2bit_equal u_2bit_equal_2 (.out_3(n2bit_equal_2_out_3), .in_1(E1), .in_2(2'b01));
  registro_paralelo registro_paralelo_2 (
    .in_3(transistor_2_out), .out_4(registro_paralelo_2_out_4), .in_1(E));  // open: in_2
  Transistor #(.\type ("n"), .width(8)) transistor_2 (
    .in(Registro), .out(transistor_2_out), .gate(n2bit_equal_2_out_3));
  _2bit_equal u_2bit_equal_3 (.out_3(n2bit_equal_3_out_3), .in_1(E1), .in_2(2'b10));
  registro_paralelo registro_paralelo_3 (
    .in_3(transistor_3_out), .out_4(registro_paralelo_3_out_4), .in_1(E));  // open: in_2
  Transistor #(.\type ("n"), .width(8)) transistor_3 (
    .in(Registro), .out(transistor_3_out), .gate(n2bit_equal_3_out_3));
  _2bit_equal u_2bit_equal_4 (.out_3(n2bit_equal_4_out_3), .in_1(E1), .in_2(2'b11));
  registro_paralelo registro_paralelo_4 (
    .in_3(transistor_4_out), .out_4(registro_paralelo_4_out_4), .in_1(E));  // open: in_2
  Transistor #(.\type ("n"), .width(8)) transistor_4 (
    .in(Registro), .out(transistor_4_out), .gate(n2bit_equal_4_out_3));
  _2bit_equal u_2bit_equal_5 (.out_3(n2bit_equal_5_out_3), .in_1(L1), .in_2(2'b00));
  Transistor #(.\type ("n"), .width(8)) transistor_5 (
    .in(registro_paralelo_1_out_4), .out(out_6), .gate(n2bit_equal_5_out_3));
  _2bit_equal u_2bit_equal_6 (.out_3(n2bit_equal_6_out_3), .in_1(L1), .in_2(2'b01));
  Transistor #(.\type ("n"), .width(8)) transistor_6 (
    .in(registro_paralelo_2_out_4), .out(out_6), .gate(n2bit_equal_6_out_3));
  _2bit_equal u_2bit_equal_7 (.out_3(n2bit_equal_7_out_3), .in_1(L1), .in_2(2'b10));
  Transistor #(.\type ("n"), .width(8)) transistor_7 (
    .in(registro_paralelo_3_out_4), .out(out_6), .gate(n2bit_equal_7_out_3));
  _2bit_equal u_2bit_equal_8 (.out_3(n2bit_equal_8_out_3), .in_1(L1), .in_2(2'b11));
  Transistor #(.\type ("n"), .width(8)) transistor_8 (
    .in(registro_paralelo_4_out_4), .out(out_6), .gate(n2bit_equal_8_out_3));
  _2bit_equal u_2bit_equal_9 (.out_3(n2bit_equal_9_out_3), .in_1(L2), .in_2(2'b00));
  Transistor #(.\type ("n"), .width(8)) transistor_9 (
    .in(registro_paralelo_1_out_4), .out(out_7), .gate(n2bit_equal_9_out_3));
  _2bit_equal u_2bit_equal_10 (.out_3(n2bit_equal_10_out_3), .in_1(L2), .in_2(2'b01));
  Transistor #(.\type ("n"), .width(8)) transistor_10 (
    .in(registro_paralelo_2_out_4), .out(out_7), .gate(n2bit_equal_10_out_3));
  _2bit_equal u_2bit_equal_11 (.out_3(n2bit_equal_11_out_3), .in_1(L2), .in_2(2'b10));
  Transistor #(.\type ("n"), .width(8)) transistor_11 (
    .in(registro_paralelo_3_out_4), .out(out_7), .gate(n2bit_equal_11_out_3));
  _2bit_equal u_2bit_equal_12 (.out_3(n2bit_equal_12_out_3), .in_1(L2), .in_2(2'b11));
  Transistor #(.\type ("n"), .width(8)) transistor_12 (
    .in(registro_paralelo_4_out_4), .out(out_7), .gate(n2bit_equal_12_out_3));
endmodule

module _2bit_equal (
  input  [1:0] in_1,
  input  [1:0] in_2,
  output out_3
);

  wire bit_equal_1_out_3, bit_equal_2_out_3;

  bit_equal bit_equal_1 (.in_1(in_2[0]), .in_2(in_1[0]), .out_3(bit_equal_1_out_3));
  bit_equal bit_equal_2 (.in_1(in_2[1]), .in_2(in_1[1]), .out_3(bit_equal_2_out_3));
  and and_1 (out_3, bit_equal_1_out_3, bit_equal_2_out_3);
endmodule

module banco_alu (
  input  [15:0] in_1,
  output [7:0] Resultado,
  output Desbordamiento
);

  wire clock_1_out, not_1_out;
  wire [7:0] banco_registros_1_out_6, banco_registros_1_out_7, transistor_1_out, undriven;

  not not_1 (not_1_out, in_1[8]);
  Clock clock_1 (.out(clock_1_out));
  Transistor #(.\type ("n"), .gate("br"), .width(8)) transistor_1 (
    .in(banco_registros_1_out_7), .out(transistor_1_out), .gate(not_1_out));
  banco_registros banco_registros_1 (
    .L1(in_1[10:9]), .L2(in_1[1:0]), .out_6(banco_registros_1_out_6), .out_7(banco_registros_1_out_7),
    .Registro(undriven), .E1(in_1[12:11]), .E(clock_1_out));
  Transistor #(.\type ("n"), .width(8)) transistor_2 (.in(in_1[7:0]), .out(transistor_1_out), .gate(in_1[8]));
  registro_paralelo registro_paralelo_1 (.in_3(undriven), .out_4(Resultado), .in_1(clock_1_out));  // open: in_2
  ALU_Spliter alu_spliter_1 (
    .A(banco_registros_1_out_6), .B(transistor_1_out), .out_4(Resultado), .Desborde(Desbordamiento),
    .in_1(in_1[15:13]));
endmodule
