// Logisim project comp.circ as structural Verilog: 4 circuits, main circuit main
module main (
);

  wire and_1_out_3, and_2_out_3, not_1_out_2, not_2_out_2, not_3_out_2, or_1_out_3, or_2_out_3;

  Not not_1 (.in_1(1'b1), .out_2(not_1_out_2));
  Not not_2 (.in_1(1'b1), .out_2(not_2_out_2));
  Not not_3 (.in_1(1'b1), .out_2(not_3_out_2));
  Or or_1 (.in_1(not_1_out_2), .in_2(1'b1), .out_3(or_1_out_3));
  And and_1 (.in_1(1'b1), .in_2(not_2_out_2), .out_3(and_1_out_3));
  And and_2 (.in_1(not_3_out_2), .in_2(1'b1), .out_3(and_2_out_3));
  Or or_2 (.in_1(and_1_out_3), .in_2(and_2_out_3), .out_3(or_2_out_3));
  LED led_1 (.in(or_1_out_3));
  LED led_2 (.in(or_2_out_3));

  // Notes on the sheet:
  //   1
  //   2
  //   A
  //   B
endmodule

module And (
  input  in_1,
  input  in_2,
  output out_3
);

  wire transistor_1_out;

  Transistor #(.\type ("n")) transistor_1 (.in(1'b1), .out(transistor_1_out), .gate(in_2));
  Transistor transistor_2 (.in(1'b0), .out(out_3), .gate(in_2));
  Transistor transistor_3 (.in(1'b0), .out(out_3), .gate(in_1));
  Transistor #(.\type ("n")) transistor_4 (.in(transistor_1_out), .out(out_3), .gate(in_1));
endmodule

module Or (
  input  in_1,
  input  in_2,
  output out_3
);

  Transistor #(.\type ("n")) transistor_1 (.in(1'b1), .out(out_3), .gate(in_1));
  Transistor transistor_2 (.in(in_2), .out(out_3), .gate(in_1));
endmodule

module Not (
  input  in_1,
  output out_2
);

  Transistor transistor_1 (.in(1'b1), .out(out_2), .gate(in_1));
  Transistor #(.\type ("n")) transistor_2 (.in(1'b0), .out(out_2), .gate(in_1));
endmodule
