// Logisim project practica4.circ as structural Verilog
module bit_equal (
  input  in_1,
  input  in_2,
  output out_3
);

  xnor xnor_1 (out_3, in_1, in_2);
endmodule

module _3bit_equal (
  input  in_1,
  input  in_2,
  input  in_3,
  input  in_4,
  input  in_5,
  input  in_6,
  output out_7
);

  wire bit_equal_1_out_3, bit_equal_2_out_3, bit_equal_3_out_3;

  bit_equal bit_equal_1 (.in_1(in_1), .in_2(in_2), .out_3(bit_equal_1_out_3));
  bit_equal bit_equal_2 (.in_1(in_3), .in_2(in_4), .out_3(bit_equal_2_out_3));
  bit_equal bit_equal_3 (.in_1(in_5), .in_2(in_6), .out_3(bit_equal_3_out_3));
  and and_1 (out_7, bit_equal_1_out_3, bit_equal_2_out_3, bit_equal_3_out_3);
endmodule

module bit_add (
  input  in_1,
  input  in_2,
  input  in_3,
  output out_4,
  output out_5
);

  wire and_1_out, and_2_out, xor_1_out;

  and and_1 (and_1_out, in_3, in_2);
  xor xor_1 (xor_1_out, in_2, in_3);
  and and_2 (and_2_out, xor_1_out, in_1);
  xor xor_2 (out_4, in_1, xor_1_out);
  or or_1 (out_5, and_2_out, and_1_out);
endmodule

module ALU (
  input  A,
  input  B,
  input  C_i,
  input  Op,
  input  in_5,
  input  in_6,
  output S,
  output C_i_1
);

  wire and_1_out, and_2_out, and_3_out, and_4_out, and_5_out, bit_add_1_out_4, bit_add_1_out_5,
       n3bit_equal_1_out_7, n3bit_equal_2_out_7, n3bit_equal_3_out_7, n3bit_equal_4_out_7, nor_1_out,
       or_1_out, or_3_out, or_4_out;

  _3bit_equal u_3bit_equal_1 (
    .in_2(Op), .in_4(in_5), .in_6(in_6), .out_7(n3bit_equal_1_out_7), .in_1(1'b0), .in_3(1'b0), .in_5(1'b0));
  _3bit_equal u_3bit_equal_2 (
    .in_2(Op), .in_4(in_5), .in_6(in_6), .out_7(n3bit_equal_2_out_7), .in_1(1'b0), .in_3(1'b0), .in_5(1'b1));
  _3bit_equal u_3bit_equal_3 (
    .in_2(Op), .in_4(in_5), .in_6(in_6), .out_7(n3bit_equal_3_out_7), .in_1(1'b0), .in_3(1'b1), .in_5(1'b0));
  _3bit_equal u_3bit_equal_4 (
    .in_2(Op), .in_4(in_5), .in_6(in_6), .out_7(n3bit_equal_4_out_7), .in_1(1'b1), .in_3(1'b1), .in_5(1'b0));
  bit_add bit_add_1 (.in_2(A), .in_3(B), .out_4(bit_add_1_out_4), .out_5(bit_add_1_out_5), .in_1(C_i));
  and and_1 (and_1_out, B, A);
  or or_1 (or_1_out, B, A);
  nor nor_1 (nor_1_out, B, A);
  or or_2 (S, and_2_out, or_3_out);
  and and_2 (and_2_out, n3bit_equal_1_out_7, and_1_out);
  or or_3 (or_3_out, and_3_out, or_4_out);
  and and_3 (and_3_out, n3bit_equal_2_out_7, or_1_out);
  or or_4 (or_4_out, and_4_out, and_5_out);
  and and_4 (and_4_out, n3bit_equal_3_out_7, nor_1_out);
  and and_5 (and_5_out, n3bit_equal_4_out_7, bit_add_1_out_4);
  and and_6 (C_i_1, n3bit_equal_4_out_7, bit_add_1_out_5);
endmodule

module _8_bit_ALU (
  input  in_1,
  input  in_2,
  input  in_3,
  input  in_4,
  input  in_5,
  input  in_6,
  input  in_7,
  input  in_8,
  input  in_9,
  input  in_10,
  input  in_11,
  input  in_12,
  input  in_13,
  input  in_14,
  input  in_15,
  input  in_16,
  input  in_17,
  input  in_18,
  input  in_19,
  output out_20,
  output out_21,
  output out_22,
  output out_23,
  output out_24,
  output out_25,
  output out_26,
  output out_27,
  output out_28
);

  wire alu_1_c_i_1, alu_2_c_i_1, alu_3_c_i_1, alu_4_c_i_1, alu_5_c_i_1, alu_6_c_i_1, alu_7_c_i_1;

  ALU alu_1 (.A(in_4), .B(in_5), .C_i(1'b0), .Op(in_1), .in_5(in_2), .in_6(in_3), .S(out_20), .C_i_1(alu_1_c_i_1));
  ALU alu_2 (
    .A(in_6), .B(in_7), .C_i(alu_1_c_i_1), .Op(in_1), .in_5(in_2), .in_6(in_3), .S(out_21),
    .C_i_1(alu_2_c_i_1));
  ALU alu_3 (
    .A(in_8), .B(in_9), .C_i(alu_2_c_i_1), .Op(in_1), .in_5(in_2), .in_6(in_3), .S(out_22),
    .C_i_1(alu_3_c_i_1));
  ALU alu_4 (
    .A(in_10), .B(in_11), .C_i(alu_3_c_i_1), .Op(in_1), .in_5(in_2), .in_6(in_3), .S(out_23),
    .C_i_1(alu_4_c_i_1));
  ALU alu_5 (
    .A(in_12), .B(in_13), .C_i(alu_4_c_i_1), .Op(in_1), .in_5(in_2), .in_6(in_3), .S(out_24),
    .C_i_1(alu_5_c_i_1));
  ALU alu_6 (
    .A(in_14), .B(in_15), .C_i(alu_5_c_i_1), .Op(in_1), .in_5(in_2), .in_6(in_3), .S(out_25),
    .C_i_1(alu_6_c_i_1));
  ALU alu_7 (
    .A(in_16), .B(in_17), .C_i(alu_6_c_i_1), .Op(in_1), .in_5(in_2), .in_6(in_3), .S(out_26),
    .C_i_1(alu_7_c_i_1));
  ALU alu_8 (.A(in_18), .B(in_19), .C_i(alu_7_c_i_1), .Op(in_1), .in_5(in_2), .in_6(in_3), .S(out_27), .C_i_1(out_28));
endmodule

module ALU_2 (
  input  in_1,
  input  in_2,
  input  in_3,
  input  B,
  input  in_5,
  input  in_6,
  input  in_7,
  input  in_8,
  input  in_9,
  input  in_10,
  input  in_11,
  input  in_12,
  input  in_13,
  input  in_14,
  input  in_15,
  input  in_16,
  input  in_17,
  input  in_18,
  input  in_19,
  output out_20,
  output out_21,
  output out_22,
  output out_23,
  output out_24,
  output out_25,
  output out_26,
  output out_27,
  output out_28
);

  wire n3bit_equal_1_out_7, n8_bit_alu_1_out_20, n8_bit_alu_1_out_21, n8_bit_alu_1_out_22,
       n8_bit_alu_1_out_23, n8_bit_alu_1_out_24, n8_bit_alu_1_out_25, n8_bit_alu_1_out_26,
       n8_bit_alu_1_out_27, xor_1_out, xor_2_out, xor_3_out, xor_4_out, xor_5_out, xor_6_out, xor_7_out,
       xor_8_out, xor_9_out;

  _3bit_equal u_3bit_equal_1 (
    .in_2(in_3), .in_4(in_2), .in_6(in_1), .out_7(n3bit_equal_1_out_7), .in_1(1'b1), .in_3(1'b1), .in_5(1'b1));
  xor xor_1 (xor_1_out, n3bit_equal_1_out_7, B);
  xor xor_2 (xor_2_out, n3bit_equal_1_out_7, in_5);
  xor xor_3 (xor_3_out, n3bit_equal_1_out_7, in_6);
  xor xor_4 (xor_4_out, n3bit_equal_1_out_7, in_8);
  xor xor_5 (xor_5_out, n3bit_equal_1_out_7, in_11);
  xor xor_6 (xor_6_out, n3bit_equal_1_out_7, in_14);
  xor xor_7 (xor_7_out, n3bit_equal_1_out_7, in_17);
  xor xor_8 (xor_8_out, n3bit_equal_1_out_7, in_19);
  _8_bit_ALU u_8_bit_alu_1 (
    .in_4(n3bit_equal_1_out_7), .in_5(xor_1_out), .in_6(1'b0), .in_7(xor_2_out), .in_10(1'b0),
    .in_11(xor_4_out), .in_12(1'b0), .in_13(xor_5_out), .in_14(1'b0), .in_15(xor_6_out), .in_16(1'b0),
    .in_17(xor_7_out), .out_20(n8_bit_alu_1_out_20), .out_21(n8_bit_alu_1_out_21),
    .out_23(n8_bit_alu_1_out_23), .out_24(n8_bit_alu_1_out_24), .out_25(n8_bit_alu_1_out_25),
    .out_26(n8_bit_alu_1_out_26), .in_1(1'b1), .in_2(1'b1), .in_3(1'b0), .in_8(1'b0),
    .out_22(n8_bit_alu_1_out_22), .in_9(xor_3_out), .in_18(1'b0), .out_27(n8_bit_alu_1_out_27),
    .in_19(xor_8_out));  // open: out_28
  xor xor_9 (xor_9_out, n3bit_equal_1_out_7, in_3);
  _8_bit_ALU u_8_bit_alu_2 (
    .in_4(n8_bit_alu_1_out_20), .in_5(in_7), .in_6(n8_bit_alu_1_out_21), .in_7(in_9),
    .in_10(n8_bit_alu_1_out_23), .in_11(in_12), .in_12(n8_bit_alu_1_out_24), .in_13(in_13),
    .in_14(n8_bit_alu_1_out_25), .in_15(in_15), .in_16(n8_bit_alu_1_out_26), .in_17(in_16), .out_20(out_20),
    .out_21(out_21), .out_23(out_23), .out_24(out_24), .out_25(out_25), .out_26(out_26), .in_1(in_1),
    .in_2(in_2), .in_3(xor_9_out), .out_28(out_28), .in_8(n8_bit_alu_1_out_22), .out_22(out_22),
    .in_9(in_10), .in_18(n8_bit_alu_1_out_27), .out_27(out_27), .in_19(in_18));
endmodule
